# Fritzing sketch LEDRACE (saved by Fritzing 0.9.3b)
breadboards: 1

parts:
  Part1 = Arduino Nano (Rev3.0)
  NEOPIXEL1 = Neopixel Strip -- White (60/m)
  R1 = Resistor [tolerance=±5% resistance=470 package=THT]
  C1 = Capacitor Polarized [package=cpol-radial-1000uf-63v]
  Power_plug1 = Power plug
  S1 = Square Pushbutton
  R2 = Resistor [tolerance=±5% resistance=10k package=THT]
  S2 = Square Pushbutton
  R3 = Resistor [tolerance=±5% resistance=10k package=THT]

nets:
  GND: Part1.GND, NEOPIXEL1.GND, C1.-, Power_plug1.GND, R2.Pin_1, R3.Pin_1
  N1: Part1.D6, R1.Pin_0
  N2: Part1.D7, S1.leg0, R2.Pin_0
  N3: Part1.D8, S2.leg1, R3.Pin_0
  5V: Part1.5V, NEOPIXEL1.DI, C1.+, Power_plug1.VCC, S1.leg1, S2.leg0
  N4: NEOPIXEL1.+5V, R1.Pin_1

custom parts:
  Neopixel Strip -- White (60/m): Neopixel Strip, White, 60 pixels per meter.

// code stored in the sketch: Untitled2.ino
/*
  Blink

  Turns an LED on for one second, then off for one second, repeatedly.

  Most Arduinos have an on-board LED you can control. On the UNO, MEGA and ZERO
  it is attached to digital pin 13, on MKR1000 on pin 6. LED_BUILTIN is set to
  the correct LED pin independent of which board is used.
  If you want to know what pin the on-board LED is connected to on your Arduino
  model, check the Technical Specs of your board at:
  https://www.arduino.cc/en/Main/Products

  modified 8 May 2014
  by Scott Fitzgerald
  modified 2 Sep 2016
  by Arturo Guadalupi
  modified 8 Sep 2016
  by Colby Newman

  This example code is in the public domain.

  http://www.arduino.cc/en/Tutorial/Blink
*/

// the setup function runs once when you press reset or power the board
void setup() {
  // initialize digital pin LED_BUILTIN as an output.
  pinMode(LED_BUILTIN, OUTPUT);
}

// the loop function runs over and over again forever
void loop() {
  digitalWrite(LED_BUILTIN, HIGH);   // turn the LED on (HIGH is the voltage level)
  delay(1000);                       // wait for a second
  digitalWrite(LED_BUILTIN, LOW);    // turn the LED off by making the voltage LOW
  delay(1000);                       // wait for a second
}
